// Logisim project e2575983.circ as structural Verilog: 1 circuit, main circuit main
module main (
  input  A1,
  input  A0,
  input  B1,
  input  B0,
  input  O3,
  input  O2,
  input  O1,
  input  O0,
  output G,
  output E,
  output L,
  output C,
  output S,
  output P,
  output Z,
  output L0,
  output L1,
  output L2,
  output L3,
  output L4,
  output L5,
  output L6,
  output L7,
  output L8,
  output L9
);

  wire and_1_out, and_2_out, and_3_out, and_4_out, and_5_out, and_6_out, and_7_out, and_8_out, and_9_out,
       and_10_out, and_11_out, and_12_out, and_13_out, and_14_out, and_15_out, and_16_out, and_17_out,
       and_18_out, and_19_out, and_20_out, and_21_out, and_22_out, and_23_out, and_24_out, and_25_out,
       and_26_out, and_27_out, and_28_out, and_29_out, and_30_out, controlled_buffer_1_out,
       controlled_buffer_3_out, controlled_buffer_5_out, n3_to_8_decoder_74138_1_p4,
       n3_to_8_decoder_74138_1_p5, n3_to_8_decoder_74138_1_p6, n3_to_8_decoder_74138_2_p7,
       n3_to_8_decoder_74138_2_p8, n3_to_8_decoder_74138_2_p9, n3_to_8_decoder_74138_2_p10,
       n3_to_8_decoder_74138_2_p11, n3_to_8_decoder_74138_2_p12, n3_to_8_decoder_74138_2_p15,
       n3_to_8_decoder_74138_2_p16, n3_to_8_decoder_74138_2_p17, n3_to_8_decoder_74138_2_p18,
       n3_to_8_decoder_74138_2_p19, n3_to_8_decoder_74138_2_p20, n3_to_8_decoder_74138_2_p21,
       n3_to_8_decoder_74138_2_p22, n3_to_8_decoder_74138_3_p4, n3_to_8_decoder_74138_3_p5,
       n3_to_8_decoder_74138_3_p6, n3_to_8_decoder_74138_3_p7, n3_to_8_decoder_74138_3_p8,
       n3_to_8_decoder_74138_3_p9, n3_to_8_decoder_74138_3_p10, n3_to_8_decoder_74138_3_p11,
       n3_to_8_decoder_74138_3_p12, n3_to_8_decoder_74138_3_p13, n3_to_8_decoder_74138_3_p14,
       n3_to_8_decoder_74138_4_p10, n3_to_8_decoder_74138_4_p11, n3_to_8_decoder_74138_4_p12,
       n3_to_8_decoder_74138_4_p13, n3_to_8_decoder_74138_4_p14, n3_to_8_decoder_74138_4_p15,
       n3_to_8_decoder_74138_4_p16, n3_to_8_decoder_74138_4_p17, n3_to_8_decoder_74138_4_p18,
       n3_to_8_decoder_74138_4_p19, n3_to_8_decoder_74138_4_p20, n3_to_8_decoder_74138_4_p21,
       n3_to_8_decoder_74138_4_p22, n3_to_8_decoder_74138_4_p23, n3_to_8_decoder_74138_4_p24,
       n3_to_8_decoder_74138_4_p25, n3_to_8_decoder_74138_4_p26, n3_to_8_decoder_74138_4_p27,
       n3_to_8_decoder_74138_5_p6, n3_to_8_decoder_74138_5_p7, n3_to_8_decoder_74138_5_p8,
       n3_to_8_decoder_74138_5_p9, n3_to_8_decoder_74138_5_p10, n3_to_8_decoder_74138_5_p11,
       n3_to_8_decoder_74138_5_p12, n3_to_8_decoder_74138_5_p13, n3_to_8_decoder_74138_6_p5,
       n3_to_8_decoder_74138_6_p10, n3_to_8_decoder_74138_6_p11, n3_to_8_decoder_74138_6_p12,
       n3_to_8_decoder_74138_6_p13, n3_to_8_decoder_74138_6_p14, n3_to_8_decoder_74138_6_p15,
       n3_to_8_decoder_74138_6_p16, n3_to_8_decoder_74138_6_p17, n3_to_8_decoder_74138_6_p18,
       n3_to_8_decoder_74138_6_p19, n3_to_8_decoder_74138_6_p20, n3_to_8_decoder_74138_6_p21,
       n3_to_8_decoder_74138_6_p22, n3_to_8_decoder_74138_6_p23, n4_to_1_mux_x2_74153_1_p10,
       n4_to_1_mux_x2_74153_1_p11, n4_to_1_mux_x2_74153_2_p13, n4_to_1_mux_x2_74153_2_p14,
       n4_to_1_mux_x2_74153_3_p13, n4_to_1_mux_x2_74153_3_p14, n4_to_1_mux_x2_74153_4_p22,
       n4_to_1_mux_x2_74153_4_p23, n4_to_1_mux_x2_74153_4_p24, n4_to_1_mux_x2_74153_4_p25,
       n4_to_1_mux_x2_74153_4_p26, n4_to_1_mux_x2_74153_4_p27, not_1_out, not_2_out, not_3_out, not_4_out,
       not_5_out, not_6_out, not_8_out, not_9_out, not_10_out, not_11_out, not_12_out, not_13_out,
       not_14_out, not_15_out, not_16_out, not_17_out, not_18_out, not_19_out, not_20_out, not_21_out,
       not_22_out, not_23_out, not_24_out, not_25_out, not_26_out, not_27_out, not_28_out, not_29_out,
       not_30_out, not_31_out, not_32_out, not_36_out, not_37_out, not_38_out, not_49_out, or_1_out,
       or_2_out, or_3_out, or_4_out, or_5_out, or_6_out, or_7_out, or_8_out, or_9_out, or_10_out, or_11_out,
       or_12_out, or_13_out, or_14_out, or_15_out, or_16_out, or_17_out, or_18_out, or_19_out, or_20_out,
       or_21_out, or_22_out, xor_1_out, xor_2_out, xor_3_out, xor_4_out, xor_5_out, xor_6_out, xor_7_out,
       xor_8_out, xor_9_out, xor_10_out, xor_11_out;

  not not_1 (not_1_out, A1);
  not not_2 (not_2_out, A0);
  not not_3 (not_3_out, B1);
  not not_4 (not_4_out, B0);
  xor xor_1 (xor_1_out, B1, n3_to_8_decoder_74138_2_p7);
  and and_1 (and_1_out, xor_1_out, not_10_out);
  or or_1 (or_1_out, and_1_out, and_16_out);
  and and_2 (and_2_out, not_2_out, B0);
  and and_3 (and_3_out, not_4_out, A0);
  and and_4 (and_4_out, B1, not_1_out);
  and and_5 (and_5_out, not_1_out, A0);
  and and_6 (and_6_out, A0, B1);
  and and_7 (and_7_out, A1, not_2_out);
  and and_8 (and_8_out, A0, B0);
  and and_9 (and_9_out, A1, B0);
  and and_10 (and_10_out, A0, B1);
  and and_11 (and_11_out, A1, B1);
  and and_12 (and_12_out, A0, not_3_out);
  and and_13 (and_13_out, A1, B1);
  and and_14 (and_14_out, A1, A0);
  and and_15 (and_15_out, A1, not_3_out);
  // _3_to_8_decoder__74138 #(.Facing("east")) 3_to_8_decoder_74138_1: pin names not known; wires that end beside it: B0, B1, A0, n3_to_8_decoder_74138_1_p4, n3_to_8_decoder_74138_1_p5, n3_to_8_decoder_74138_1_p6
  not not_5 (not_5_out, A1);
  and and_16 (and_16_out, B1, n3_to_8_decoder_74138_2_p7);
  or or_2 (or_2_out, B0, A0);
  xor xor_2 (xor_2_out, xor_1_out, not_10_out);
  xor xor_3 (xor_3_out, A0, B0);
  and and_17 (and_17_out, and_2_out, not_6_out);
  not not_6 (not_6_out, xor_4_out);
  xor xor_4 (xor_4_out, A1, B1);
  and and_18 (and_18_out, B0, A0);
  and and_19 (and_19_out, A1, B1);
  or or_3 (or_3_out, B0, A0);
  or or_4 (or_4_out, A1, B1);
  xor xor_5 (xor_5_out, A0, B0);
  xor xor_6 (xor_6_out, A1, B1);
  and and_20 (and_20_out, and_5_out, B1);
  or or_5 (or_5_out, and_20_out, and_21_out);
  and and_21 (and_21_out, and_6_out, not_4_out);
  and and_22 (and_22_out, and_7_out, B1);
  and and_23 (and_23_out, and_22_out, B0);
  and and_24 (and_24_out, and_12_out, B0);
  or or_6 (or_6_out, and_24_out, and_25_out);
  and and_25 (and_25_out, and_13_out, not_4_out);
  and and_26 (and_26_out, and_14_out, B0);
  and and_27 (and_27_out, and_15_out, B0);
  // _3_to_8_decoder__74138 #(.Facing("east")) 3_to_8_decoder_74138_2: pin names not known; wires that end beside it: not_5_out, 1'b0, 1'b0, B0, B1, A0, n3_to_8_decoder_74138_2_p7, n3_to_8_decoder_74138_2_p8, n3_to_8_decoder_74138_2_p9, n3_to_8_decoder_74138_2_p10, n3_to_8_decoder_74138_2_p11, n3_to_8_decoder_74138_2_p12, 1'b0, 1'b0, n3_to_8_decoder_74138_2_p15, n3_to_8_decoder_74138_2_p16, n3_to_8_decoder_74138_2_p17, n3_to_8_decoder_74138_2_p18, n3_to_8_decoder_74138_2_p19, n3_to_8_decoder_74138_2_p20, n3_to_8_decoder_74138_2_p21, n3_to_8_decoder_74138_2_p22
  not not_7 (n3_to_8_decoder_74138_2_p7, not_5_out);
  not not_8 (not_8_out, B0);
  not not_9 (not_9_out, A0);
  or or_7 (or_7_out, not_8_out, not_9_out);
  and and_28 (and_28_out, or_2_out, or_7_out);
  not not_10 (not_10_out, or_7_out);
  xor xor_7 (xor_7_out, controlled_buffer_1_out, xor_4_out);
  or or_8 (or_8_out, and_17_out, and_4_out);
  xor xor_8 (xor_8_out, and_9_out, and_10_out);
  and and_29 (and_29_out, and_10_out, and_9_out);
  xor xor_9 (xor_9_out, and_29_out, and_11_out);
  and and_30 (and_30_out, and_11_out, and_29_out);
  or or_9 (or_9_out, or_6_out, and_26_out);
  not not_11 (not_11_out, n3_to_8_decoder_74138_1_p4);
  not not_12 (not_12_out, n3_to_8_decoder_74138_1_p5);
  not not_13 (not_13_out, n3_to_8_decoder_74138_1_p6);
  or or_10 (or_10_out, not_12_out, not_14_out);
  not not_14 (not_14_out, n3_to_8_decoder_74138_2_p8);
  not not_15 (not_15_out, n3_to_8_decoder_74138_2_p9);
  not not_16 (not_16_out, n3_to_8_decoder_74138_2_p10);
  not not_17 (not_17_out, n3_to_8_decoder_74138_2_p11);
  not not_18 (not_18_out, n3_to_8_decoder_74138_2_p12);
  or or_11 (or_11_out, not_18_out, not_22_out);
  not not_19 (not_19_out, n3_to_8_decoder_74138_2_p15);
  not not_20 (not_20_out, n3_to_8_decoder_74138_2_p16);
  not not_21 (not_21_out, n3_to_8_decoder_74138_2_p17);
  not not_22 (not_22_out, n3_to_8_decoder_74138_2_p18);
  not not_23 (not_23_out, n3_to_8_decoder_74138_2_p19);
  not not_24 (not_24_out, n3_to_8_decoder_74138_2_p20);
  not not_25 (not_25_out, n3_to_8_decoder_74138_2_p21);
  not not_26 (not_26_out, n3_to_8_decoder_74138_2_p22);
  or or_12 (or_12_out, not_13_out, or_10_out);
  or or_13 (or_13_out, or_12_out, or_14_out);
  or or_14 (or_14_out, not_17_out, or_11_out);
  assign controlled_buffer_1_out = not_27_out ? and_3_out : 1'bz;  // Controlled_Buffer controlled_buffer_1
  assign controlled_buffer_1_out = not_28_out ? and_2_out : 1'bz;  // Controlled_Buffer controlled_buffer_2
  assign controlled_buffer_3_out = O3 ? or_4_out : 1'bz;  // Controlled_Buffer controlled_buffer_3
  assign controlled_buffer_3_out = not_29_out ? and_23_out : 1'bz;  // Controlled_Buffer controlled_buffer_4
  or or_15 (or_15_out, not_11_out, not_16_out);
  or or_16 (or_16_out, not_26_out, not_21_out);
  or or_17 (or_17_out, not_15_out, not_19_out);
  not not_27 (not_27_out, not_28_out);
  not not_28 (not_28_out, or_8_out);
  or or_18 (or_18_out, or_15_out, or_16_out);
  or or_19 (or_19_out, or_17_out, or_20_out);
  or or_20 (or_20_out, not_20_out, not_23_out);
  or or_21 (or_21_out, or_19_out, or_22_out);
  or or_22 (or_22_out, not_24_out, not_25_out);
  not not_29 (not_29_out, O3);
  not not_30 (not_30_out, O2);
  not not_31 (not_31_out, O1);
  not not_32 (not_32_out, O0);
  and and_31 (L, or_13_out, not_38_out);
  and and_32 (G, or_21_out, not_38_out);
  assign controlled_buffer_5_out = O3 ? or_3_out : 1'bz;  // Controlled_Buffer controlled_buffer_5
  assign controlled_buffer_5_out = not_29_out ? or_5_out : 1'bz;  // Controlled_Buffer controlled_buffer_6
  // _4_to_1_MUX__x2___74153 #(.Facing("east")) 4_to_1_mux_x2_74153_1: pin names not known; wires that end beside it: xor_3_out, 1'b0, and_18_out, xor_5_out, controlled_buffer_5_out, and_8_out, or_9_out, not_30_out, O2, n4_to_1_mux_x2_74153_1_p10, n4_to_1_mux_x2_74153_1_p11
  // _4_to_1_MUX__x2___74153 #(.Facing("east")) 4_to_1_mux_x2_74153_2: pin names not known; wires that end beside it: and_28_out, xor_7_out, 1'b0, and_19_out, xor_6_out, controlled_buffer_3_out, xor_8_out, and_27_out, O0, not_30_out, O1, O2, n4_to_1_mux_x2_74153_2_p13, n4_to_1_mux_x2_74153_2_p14
  // _4_to_1_MUX__x2___74153 #(.Facing("east")) 4_to_1_mux_x2_74153_3: pin names not known; wires that end beside it: xor_2_out, 1'b0, 1'b0, 1'b0, 1'b0, 1'b0, xor_9_out, 1'b0, O0, not_30_out, O1, O2, n4_to_1_mux_x2_74153_3_p13, n4_to_1_mux_x2_74153_3_p14
  // _4_to_1_MUX__x2___74153 #(.Facing("east")) 4_to_1_mux_x2_74153_4: pin names not known; wires that end beside it: O2, not_30_out, O1, not_31_out, O0, not_32_out, or_1_out, 1'b0, 1'b0, 1'b0, 1'b0, 1'b0, and_30_out, 1'b0, 1'b0, O0, not_30_out, O0, O1, O2, O1, n4_to_1_mux_x2_74153_4_p22, n4_to_1_mux_x2_74153_4_p23, n4_to_1_mux_x2_74153_4_p24, n4_to_1_mux_x2_74153_4_p25, n4_to_1_mux_x2_74153_4_p26, n4_to_1_mux_x2_74153_4_p27
  // _3_to_8_decoder__74138 #(.Facing("east")) 3_to_8_decoder_74138_3: pin names not known; wires that end beside it: O0, O1, O2, n3_to_8_decoder_74138_3_p4, n3_to_8_decoder_74138_3_p5, n3_to_8_decoder_74138_3_p6, n3_to_8_decoder_74138_3_p7, n3_to_8_decoder_74138_3_p8, n3_to_8_decoder_74138_3_p9, n3_to_8_decoder_74138_3_p10, n3_to_8_decoder_74138_3_p11, n3_to_8_decoder_74138_3_p12, n3_to_8_decoder_74138_3_p13, n3_to_8_decoder_74138_3_p14
  // _3_to_8_decoder__74138 #(.Facing("east")) 3_to_8_decoder_74138_4: pin names not known; wires that end beside it: O0, O1, O2, not_29_out, O3, 1'b0, 1'b0, 1'b0, 1'b0, n3_to_8_decoder_74138_4_p10, n3_to_8_decoder_74138_4_p11, n3_to_8_decoder_74138_4_p12, n3_to_8_decoder_74138_4_p13, n3_to_8_decoder_74138_4_p14, n3_to_8_decoder_74138_4_p15, n3_to_8_decoder_74138_4_p16, n3_to_8_decoder_74138_4_p17, n3_to_8_decoder_74138_4_p18, n3_to_8_decoder_74138_4_p19, n3_to_8_decoder_74138_4_p20, n3_to_8_decoder_74138_4_p21, n3_to_8_decoder_74138_4_p22, n3_to_8_decoder_74138_4_p23, n3_to_8_decoder_74138_4_p24, n3_to_8_decoder_74138_4_p25, n3_to_8_decoder_74138_4_p26, n3_to_8_decoder_74138_4_p27
  and and_33 (E, not_38_out, or_18_out);
  or or_23 (n4_to_1_mux_x2_74153_4_p27, n4_to_1_mux_x2_74153_1_p10, n4_to_1_mux_x2_74153_1_p11);
  or or_24 (n4_to_1_mux_x2_74153_4_p26, n4_to_1_mux_x2_74153_2_p13, n4_to_1_mux_x2_74153_2_p14);
  or or_25 (n4_to_1_mux_x2_74153_4_p25, n4_to_1_mux_x2_74153_3_p13, n4_to_1_mux_x2_74153_3_p14);
  or or_26 (n4_to_1_mux_x2_74153_4_p24, n4_to_1_mux_x2_74153_4_p22, n4_to_1_mux_x2_74153_4_p23);
  not not_33 (n3_to_8_decoder_74138_3_p11, n3_to_8_decoder_74138_3_p4);
  not not_34 (n3_to_8_decoder_74138_3_p12, n3_to_8_decoder_74138_3_p5);
  not not_35 (n3_to_8_decoder_74138_3_p13, n3_to_8_decoder_74138_3_p6);
  not not_36 (not_36_out, n3_to_8_decoder_74138_3_p7);
  not not_37 (not_37_out, n3_to_8_decoder_74138_3_p8);
  not not_38 (not_38_out, n3_to_8_decoder_74138_3_p9);
  not not_39 (n3_to_8_decoder_74138_3_p14, n3_to_8_decoder_74138_3_p10);
  not not_40 (n3_to_8_decoder_74138_4_p19, n3_to_8_decoder_74138_4_p10);
  not not_41 (n3_to_8_decoder_74138_4_p20, n3_to_8_decoder_74138_4_p11);
  not not_42 (n3_to_8_decoder_74138_4_p21, n3_to_8_decoder_74138_4_p12);
  not not_43 (n3_to_8_decoder_74138_4_p22, n3_to_8_decoder_74138_4_p13);
  not not_44 (n3_to_8_decoder_74138_4_p23, n3_to_8_decoder_74138_4_p14);
  not not_45 (n3_to_8_decoder_74138_4_p24, n3_to_8_decoder_74138_4_p15);
  not not_46 (n3_to_8_decoder_74138_4_p25, n3_to_8_decoder_74138_4_p16);
  not not_47 (n3_to_8_decoder_74138_4_p26, n3_to_8_decoder_74138_4_p17);
  not not_48 (n3_to_8_decoder_74138_4_p27, n3_to_8_decoder_74138_4_p18);
  and and_34 (C, or_1_out, not_36_out);
  not not_49 (not_49_out, n4_to_1_mux_x2_74153_4_p24);
  // _3_to_8_decoder__74138 #(.Facing("east")) 3_to_8_decoder_74138_5: pin names not known; wires that end beside it: n4_to_1_mux_x2_74153_4_p25, n4_to_1_mux_x2_74153_4_p26, n4_to_1_mux_x2_74153_4_p27, n4_to_1_mux_x2_74153_4_p26, n4_to_1_mux_x2_74153_4_p25, n3_to_8_decoder_74138_5_p6, n3_to_8_decoder_74138_5_p7, n3_to_8_decoder_74138_5_p8, n3_to_8_decoder_74138_5_p9, n3_to_8_decoder_74138_5_p10, n3_to_8_decoder_74138_5_p11, n3_to_8_decoder_74138_5_p12, n3_to_8_decoder_74138_5_p13, E
  // _3_to_8_decoder__74138 #(.Facing("east")) 3_to_8_decoder_74138_6: pin names not known; wires that end beside it: n4_to_1_mux_x2_74153_4_p27, n4_to_1_mux_x2_74153_4_p26, n4_to_1_mux_x2_74153_4_p25, not_49_out, n3_to_8_decoder_74138_6_p5, not_38_out, not_38_out, not_38_out, not_38_out, n3_to_8_decoder_74138_6_p10, n3_to_8_decoder_74138_6_p11, n3_to_8_decoder_74138_6_p12, n3_to_8_decoder_74138_6_p13, n3_to_8_decoder_74138_6_p14, n3_to_8_decoder_74138_6_p15, n3_to_8_decoder_74138_6_p16, n3_to_8_decoder_74138_6_p17, n3_to_8_decoder_74138_6_p18, n3_to_8_decoder_74138_6_p19, n3_to_8_decoder_74138_6_p20, n3_to_8_decoder_74138_6_p21, n3_to_8_decoder_74138_6_p22, n3_to_8_decoder_74138_6_p23
  not not_50 (n3_to_8_decoder_74138_6_p5, not_49_out);
  xor xor_10 (xor_10_out, n4_to_1_mux_x2_74153_4_p24, n4_to_1_mux_x2_74153_4_p25);
  xor xor_11 (xor_11_out, n4_to_1_mux_x2_74153_4_p26, n4_to_1_mux_x2_74153_4_p27);
  and and_35 (S, not_37_out, or_13_out);
  not not_51 (L0, n3_to_8_decoder_74138_5_p6);
  not not_52 (L1, n3_to_8_decoder_74138_5_p7);
  not not_53 (L2, n3_to_8_decoder_74138_5_p8);
  not not_54 (L3, n3_to_8_decoder_74138_5_p9);
  not not_55 (L4, n3_to_8_decoder_74138_5_p10);
  not not_56 (L5, n3_to_8_decoder_74138_5_p11);
  not not_57 (L6, n3_to_8_decoder_74138_5_p12);
  not not_58 (L7, n3_to_8_decoder_74138_5_p13);
  not not_59 (L8, n3_to_8_decoder_74138_6_p10);
  not not_60 (L9, n3_to_8_decoder_74138_6_p11);
  not not_61 (n3_to_8_decoder_74138_6_p18, n3_to_8_decoder_74138_6_p12);
  not not_62 (n3_to_8_decoder_74138_6_p19, n3_to_8_decoder_74138_6_p13);
  not not_63 (n3_to_8_decoder_74138_6_p20, n3_to_8_decoder_74138_6_p14);
  not not_64 (n3_to_8_decoder_74138_6_p21, n3_to_8_decoder_74138_6_p15);
  not not_65 (n3_to_8_decoder_74138_6_p22, n3_to_8_decoder_74138_6_p16);
  not not_66 (n3_to_8_decoder_74138_6_p23, n3_to_8_decoder_74138_6_p17);
  xor xor_12 (P, xor_10_out, xor_11_out);

  assign Z = L0;
endmodule
